// Logisim project 78512025_Lab3.circ as structural Verilog
module fullbitadder (
  input  A,
  input  B,
  input  Cin,
  output Sum,
  output Carry
);

  wire and_1_out, and_2_out, and_3_out, xor_1_out;

  xor xor_1 (xor_1_out, A, B);
  and and_1 (and_1_out, A, B);
  and and_2 (and_2_out, B, Cin);
  and and_3 (and_3_out, A, Cin);
  xor xor_2 (Sum, xor_1_out, Cin);
  or or_1 (Carry, and_1_out, and_2_out, and_3_out);

  // Notes on the sheet:
  //   A Single Bit Full Adder
endmodule

module fulladder2bit (
  input  [1:0] A,
  input  Init_Cin,
  input  [1:0] B,
  output [1:0] Sum,
  output final_carry_or_overflow
);

  wire fullbitadder_1_carry;

  fullbitadder fullbitadder_1 (.A(A[0]), .B(B[0]), .Cin(Init_Cin), .Sum(Sum[0]), .Carry(fullbitadder_1_carry));
  fullbitadder fullbitadder_2 (
    .A(A[1]), .B(B[1]), .Cin(fullbitadder_1_carry), .Sum(Sum[1]), .Carry(final_carry_or_overflow));

  // Notes on the sheet:
  //   A 2-bit full adder
endmodule

module addsub2bit (
  input  control,
  input  [1:0] A,
  input  [1:0] B,
  output [1:0] sum_or_difference,
  output discarded_overflow
);

  wire fullbitadder_1_carry, xor_1_out, xor_2_out;

  xor xor_1 (xor_1_out, control, B[0]);
  xor xor_2 (xor_2_out, control, B[1]);
  fullbitadder fullbitadder_1 (
    .A(A[0]), .B(xor_1_out), .Cin(control), .Sum(sum_or_difference[0]), .Carry(fullbitadder_1_carry));
  fullbitadder fullbitadder_2 (
    .A(A[1]), .B(xor_2_out), .Cin(fullbitadder_1_carry), .Sum(sum_or_difference[1]),
    .Carry(discarded_overflow));

  // Notes on the sheet:
  //   A 2-bit addsub
endmodule

module fulladder8bit (
  input  [7:0] A,
  input  Init_Cin,
  input  [7:0] B,
  output [7:0] Sum,
  output Carry
);

  wire fullbitadder_1_carry, fullbitadder_2_carry, fullbitadder_3_carry, fullbitadder_4_carry,
       fullbitadder_5_carry, fullbitadder_6_carry, fullbitadder_7_carry;

  fullbitadder fullbitadder_1 (.A(A[0]), .B(B[0]), .Cin(Init_Cin), .Sum(Sum[3]), .Carry(fullbitadder_1_carry));
  fullbitadder fullbitadder_2 (
    .A(A[2]), .B(B[1]), .Cin(fullbitadder_1_carry), .Sum(Sum[0]), .Carry(fullbitadder_2_carry));
  fullbitadder fullbitadder_3 (
    .A(A[4]), .B(B[2]), .Cin(fullbitadder_2_carry), .Sum(Sum[1]), .Carry(fullbitadder_3_carry));
  fullbitadder fullbitadder_4 (
    .A(A[6]), .B(B[3]), .Cin(fullbitadder_3_carry), .Sum(Sum[4]), .Carry(fullbitadder_4_carry));
  fullbitadder fullbitadder_5 (
    .A(A[1]), .B(B[7]), .Cin(fullbitadder_4_carry), .Sum(Sum[2]), .Carry(fullbitadder_5_carry));
  fullbitadder fullbitadder_6 (
    .A(A[7]), .B(B[6]), .Cin(fullbitadder_5_carry), .Sum(Sum[5]), .Carry(fullbitadder_6_carry));
  fullbitadder fullbitadder_7 (
    .A(A[5]), .B(B[5]), .Cin(fullbitadder_6_carry), .Sum(Sum[6]), .Carry(fullbitadder_7_carry));
  fullbitadder fullbitadder_8 (.A(A[7]), .B(B[4]), .Cin(fullbitadder_7_carry), .Sum(Sum[7]), .Carry(Carry));

  assign A[3] = A[7];
endmodule
